// Logisim project 7seg_basicgates_fin.circ as structural Verilog: 1 circuit, main circuit 7segcircuit
module _7segcircuit (
  input  D,
  input  C,
  input  B,
  input  A
);

  wire _7408_out, _7432_2_out, _7432_out, and_1_out, and_2_out, and_3_out, G_out, not_1_out, NOT_2_out,
       not_3_out, NOT_4_out, not_5_out, not_7_out, not_8_out, not_9_out, not_10_out, not_11_out, not_12_out,
       or_1_out, or_2_out, or_3_out, or_4_out, or_5_out, or_7_out, or_8_out, or_9_out, or_10_out, undriven,
       undriven_2, undriven_3, undriven_4, undriven_5, xor_1_out, xor_2_out, xor_3_out;

  not not_1 (not_1_out, xor_1_out);
  xor xor_1 (xor_1_out, C, A);
  xor xor_2 (xor_2_out, A, B);
  not NOT_2 (NOT_2_out, xor_2_out);
  not not_3 (not_3_out, B);
  and _7408 (_7408_out, not_11_out, not_3_out);
  not NOT_4 (NOT_4_out, C);
  not not_5 (not_5_out, undriven);
  // NOT_Gate not_6 is placed but not wired
  not not_7 (not_7_out, undriven_4);
  xor xor_3 (xor_3_out, not_8_out, xor_1_out);
  xor G (G_out, B, C);
  not not_8 (not_8_out, B);
  not not_9 (not_9_out, undriven_3);
  not not_10 (not_10_out, undriven_2);
  not not_11 (not_11_out, A);
  and and_1 (and_1_out, not_11_out, B);
  and and_2 (and_2_out, NOT_4_out, not_11_out);
  and and_3 (and_3_out, not_11_out, or_5_out);
  not not_12 (not_12_out, undriven_5);
  or or_1 (or_1_out, B, not_1_out);
  or or_2 (or_2_out, NOT_4_out, NOT_2_out);
  or _7432 (_7432_out, G_out, and_1_out);
  or or_3 (or_3_out, C, _7408_out);
  or or_4 (or_4_out, D, or_1_out);
  or or_5 (or_5_out, NOT_4_out, B);
  or _7432_2 (_7432_2_out, A, not_3_out);
  // OR_Gate or_6 has open pins: in0=xor_3_out, out=open
  or or_7 (or_7_out, D, _7432_out);
  or or_8 (or_8_out, or_3_out, D);
  _7_Segment_Display u_7_segment_display_1 (
    .g(or_7_out), .f(or_8_out), .a(or_4_out), .b(or_2_out), .e(and_3_out), .d(or_10_out), .c(or_9_out));  // open: dp
  or or_9 (or_9_out, C, _7432_2_out);
  or or_10 (or_10_out, xor_3_out, and_2_out);

  // Notes on the sheet:
  //   for d
  //   3rd of F
  //   latter 2 of D
endmodule
